# Fritzing sketch Componentes Hardware (saved by Fritzing 0.9.6b)

parts:
  Componente1 = Arduino Uno (Rev3)  # not connected
  M1 = DC Motor
  J1 = Basic Servo
  HC-SR04_Sensor_1 = HC-SR04 Ultrasonic Distance Sensor
  J2 = Basic Servo
  J3 = Basic Servo
  Power_plug1 = Power plug
  Componente2 = Adafruit Motor/Stepper/Servo Shield [part_number="Adafruit #1438"]
  L1 = Solenoid
  Mod2 = KY-019 5V Relay Module [package="Breakout board"]

nets:
  N1: M1.pin_1, Componente2.M1B
  N2: M1.pin_2, Componente2.M1A
  GND: J1.gnd, J2.gnd, Componente2.GND
  VCC: J1.vcc, J2.vcc, Componente2.+5V
  VCC_2: HC-SR04_Sensor_1.VCC, Power_plug1.VCC
  N3: HC-SR04_Sensor_1.TRIG, Componente2.D2
  N4: HC-SR04_Sensor_1.ECHO, Componente2.D3
  GND_2: HC-SR04_Sensor_1.GND, Power_plug1.GND
  N5: J2.pulse, Componente2.D9
  N6: J3.pulse, Componente2.D11
  N7: Componente2.D13, Mod2.S
  N8: L1.pin1, Mod2.NO
  N9: L1.pin2, Mod2.Common

notes:
  Servo MG996R
  Motor DC
  PC
  7.5 v
  5 v
  Solenoide
  Sensor Ultrasonidos
  Relé
  Shield
  Servo SG90

custom parts:
  Adafruit Motor/Stepper/Servo Shield: The original Adafruit Motorshield kit is one of our most beloved kits, which is why we decided to make something even better. We have upgraded the shield kit to make the bestest, easiest way to drive DC and Stepper motors. This shield will make quick work of your next robotics project! We kept the ability to drive up to 4 DC motors or 2 stepper motors, but added many improvements: Instead of a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
  KY-019 5V Relay Module: KY-019 5V Relay module, used to control AC circuits. (Special thanks to vanepp for fixing the PCB holes and other errors)
